// Logisim project arch_242_Logisim.circ as structural Verilog: 20 circuits, main circuit main
module main (
);

  wire CF, CLK, clock_1_out, comparator_1_eq, comparator_2_eq, F_DONE, Jump, Shutdown, T_ENAB, WD_CF, WD_CF1,
       WE_ACC, WE_CF, WE_RM, WE_TEMP, WE_TIME;
  wire [1:0] TE_TIME, WDest_IO;
  wire [2:0] Choice_RM, PCSrc, PCSrcReal;
  wire [3:0] ACC, D_RM, IOA, OPBranch, RA, RB, RD, WD_ACC, WD_IOA;
  wire [7:0] Inst, M_Addr, OPALU, TIMER, WD_TIME;
  wire [8:0] Inst9;
  wire [11:0] PC_Ret;
  wire [15:0] multiplexer_2_out, PC, PC_Imm, PC_Jump, PC_Plus1, WD_TEMP;
  wire [15:12] TEMP;
  wire [19:0] ledfile_1_out_0, ledfile_1_out_1, ledfile_1_out_2, ledfile_1_out_3, ledfile_1_out_4,
       ledfile_1_out_5, ledfile_1_out_6, ledfile_1_out_7, ledfile_1_out_8, ledfile_1_out_9;

  Clock clock_1 (.out(clock_1_out));
  Multiplexer #(.width(3)) multiplexer_1 (.in0(PCSrc), .in1(3'b111), .out(PCSrcReal), .sel(F_DONE));
  and and_1 (CLK, clock_1_out, ~Shutdown);  // AND_Gate
  // Probe on PCSrcReal
  Multiplexer #(.select(3), .width(16)) multiplexer_2 (
    .in0(PC_Plus1), .in1({PC[15:12], PC_Ret}), .in2(PC_Jump), .in7(16'h4), .out(multiplexer_2_out),
    .sel(PCSrcReal));  // open: in3, in4, in5, in6
  Adder #(.width(16)) adder_1 (.a(PC), .b(16'h1), .out(PC_Plus1));  // open: cin, cout
  Multiplexer #(.width(16)) multiplexer_3 (.in0(PC_Plus1), .in1(PC_Imm), .out(PC_Jump), .sel(Jump));
  Register #(.width(16)) u_PC (.D(multiplexer_2_out), .Q(PC), .clk(CLK));  // open: en, clr
  // Probe on PC
  InstMem instmem_1 (.Address(PC), .Inst(Inst));
  ControlUnit controlunit_1 (
    .CLK(CLK), .Inst(Inst), .PC(PC), .WE_RM(WE_RM), .WE_ACC(WE_ACC), .WE_CF(WE_CF), .WE_TEMP(WE_TEMP),
    .WE_TIME(WE_TIME), .Choice_RM(Choice_RM), .Source_PC(PCSrc), .Opcode_ALU(OPALU), .Shutdown(Shutdown),
    .WDest_IO(WDest_IO), .Inst9(Inst9), .TE_TIME(TE_TIME), .PCImm(PC_Imm), .OP_Branch(OPBranch));
  Register #(.width(4)) u_ACC (.D(WD_ACC), .en(WE_ACC), .clk(CLK), .Q(ACC));  // open: clr
  Register #(.width(1)) u_CF (.D(WD_CF), .en(WE_CF), .clk(CLK), .Q(CF));  // open: clr
  Register #(.width(16)) u_TEMP (.D(WD_TEMP), .en(WE_TEMP), .clk(CLK), .Q({TEMP, PC_Ret}));  // open: clr
  RegMemFile regmemfile_1 (
    .CLK(CLK), .WriteEnable(WE_RM), .WriteData(WD_ACC), .RegChoice(Choice_RM), .DataOut(D_RM), .RA_Out(RA),
    .RB_Out(RB), .RD_Out(RD), .Mem_Addr(M_Addr));
  RegIOFile regiofile_1 (.CLK(CLK), .WData(WD_IOA), .IOA(IOA));
  TimerFile timerfile_1 (
    .CLK(CLK), .WData(WD_TIME), .WE(WE_TIME), .TE(TE_TIME), .Timer_Out(TIMER), .Four_Done(F_DONE),
    .Is_Enabled(T_ENAB));
  // Probe on OPALU
  Multiplexer #(.width(16)) multiplexer_4 (.in0(PC_Plus1), .in1({16{1'b0}}), .out(WD_TEMP), .sel(comparator_1_eq));
  Comparator #(.mode("unsigned"), .width(3)) comparator_1 (
    .a(PCSrc), .b(3'b001), .eq(comparator_1_eq));  // open: gt, lt
  Multiplexer multiplexer_5 (.in0(WD_CF1), .in1(TEMP[12]), .out(WD_CF), .sel(comparator_2_eq));
  Comparator #(.mode("unsigned"), .width(9)) comparator_2 (.a(Inst9), .b(9'h2f), .eq(comparator_2_eq));  // open: gt, lt
  ALU alu_1 (
    .Opcode(OPALU), .Data_In(D_RM), .ACC_In(ACC), .CF_In(CF), .Time_In(TIMER), .IOA_In(IOA),
    .Nibble_Out(WD_ACC), .CF_Out(WD_CF1), .Timer_Out(WD_TIME));
  BranchChecker branchchecker_1 (
    .OPBranch(OPBranch), .ACC(ACC), .RA(RA), .RB(RB), .RD(RD), .CF(CF), .T_ENABLED(T_ENAB), .IsJump(Jump));
  Button U (.out(WD_IOA[0]));
  Button L (.out(WD_IOA[2]));
  Button D (.out(WD_IOA[1]));
  Button R (.out(WD_IOA[3]));
  LEDFile ledfile_1 (
    .CLK(CLK), .Mem_Addr(M_Addr), .W_Data(WD_ACC), .WE(WE_RM), .OUT_0(ledfile_1_out_0),
    .OUT_1(ledfile_1_out_1), .OUT_2(ledfile_1_out_2), .OUT_3(ledfile_1_out_3), .OUT_4(ledfile_1_out_4),
    .OUT_5(ledfile_1_out_5), .OUT_6(ledfile_1_out_6), .OUT_7(ledfile_1_out_7), .OUT_8(ledfile_1_out_8),
    .OUT_9(ledfile_1_out_9));
  DotMatrix #(.inputtype("row"), .matrixcols(20), .matrixrows(10)) dotmatrix_1 (
    .row0(ledfile_1_out_0), .row1(ledfile_1_out_1), .row2(ledfile_1_out_2), .row3(ledfile_1_out_3),
    .row4(ledfile_1_out_4), .row5(ledfile_1_out_5), .row6(ledfile_1_out_6), .row7(ledfile_1_out_7),
    .row8(ledfile_1_out_8), .row9(ledfile_1_out_9));

  // Other names for the same wires on the sheet: TEMP[11:0] = PC_Ret; PC_Ret[15:12] = PC[15:12]; WD_RM[3:0] = WD_ACC

  // Notes on the sheet:
  //   PC LOGIC
  //   Deprecated, part of Timer 
  //   INST ROM HERE
  //   FETCH/DECODE
  //   Currently has Snake Game Code (run at 1kHz as it is very slow)
  //   PROCESSOR STATE
  //   MEM RAM HERE
  //   ALU EXECUTE
  //   WRITEBACK
  //   INPUT/OUTPUT
endmodule

module Outer (
);

  wire [3:0] U_out;
  wire [19:0] undriven, undriven_2, undriven_3, undriven_4, undriven_5, undriven_6, undriven_7, undriven_8,
       undriven_9, undriven_10;

  Button L (.out(U_out[2]));
  Button U (.out(U_out[0]));
  Button R (.out(U_out[3]));
  Button D (.out(U_out[1]));
  main main_1 ();
  DotMatrix #(.inputtype("row"), .matrixcols(20), .matrixrows(10)) dotmatrix_1 (
    .row0(undriven), .row1(undriven_2), .row2(undriven_3), .row3(undriven_4), .row4(undriven_5),
    .row5(undriven_6), .row6(undriven_7), .row7(undriven_8), .row8(undriven_9), .row9(undriven_10));
endmodule

module ControlUnit (
  input  CLK,
  input  [7:0] Inst,
  input  [15:0] PC,
  output WE_RM,
  output WE_ACC,
  output WE_CF,
  output WE_TEMP,
  output WE_TIME,
  output [2:0] Choice_RM,
  output [2:0] Source_PC,
  output [7:0] Opcode_ALU,
  output Shutdown,
  output [1:0] WDest_IO,
  output [8:0] Inst9,
  output [1:0] TE_TIME,
  output [15:0] PCImm,
  output [3:0] OP_Branch
);

  wire and_1_out, comparator_1_eq, comparator_2_eq, comparator_3_eq, comparator_4_eq, comparator_5_eq,
       comparator_6_eq, comparator_7_eq, comparator_8_eq, comparator_9_eq, comparator_10_eq,
       comparator_11_eq, instvalidator_1_isvalid, IS_LONG, or_3_out, Shut, WE_AC1, WE_AC2, WE_CF1, WE_CF2,
       WE_RM1, WE_RM2, WE_TE1, WE_TE2, WE_TI1, WE_TI2;
  wire [1:0] TE_TIME_t, WDE_IO;
  wire [2:0] C_RM1, C_RM2, PC_SRC1, PC_SRC2;
  wire [3:3] rom_1_data;
  wire [7:0] OP1, OP2, PrevInst;

  // Probe on Inst
  ROM #(.dataWidth(16)) rom_1 (.addr(Inst), .data({OP1, C_RM1, IS_LONG, rom_1_data[3], WE_CF1, WE_AC1, WE_RM1}));
  Comparator #(.mode("unsigned"), .width(9)) comparator_1 (
    .a({Inst9[8], Inst}), .b(9'h2e), .eq(comparator_1_eq));  // open: gt, lt
  Comparator #(.mode("unsigned"), .width(9)) comparator_2 (
    .a({Inst9[8], Inst}), .b(9'h2f), .eq(comparator_2_eq));  // open: gt, lt
  Comparator #(.mode("unsigned"), .width(9)) comparator_3 (
    .a({Inst9[8], Inst}), .b(9'h32), .eq(comparator_3_eq));  // open: gt, lt
  Comparator #(.mode("unsigned"), .width(9)) comparator_4 (
    .a({Inst9[8], Inst}), .b(9'h33), .eq(comparator_4_eq));  // open: gt, lt
  Comparator #(.mode("unsigned"), .width(9)) comparator_5 (
    .a({Inst9[8], Inst}), .b(9'h34), .eq(comparator_5_eq));  // open: gt, lt
  LED led_1 (.in(instvalidator_1_isvalid));
  InstValidator instvalidator_1 (.Inst(Inst), .IsValid(instvalidator_1_isvalid));
  or or_1 (WE_TE1, comparator_1_eq, comparator_2_eq);
  Priority_Encoder #(.select(2)) priority_encoder_1 (
    .in0(1'b1), .in1(comparator_3_eq), .in2(comparator_4_eq), .in3(comparator_5_eq), .out(WDE_IO));  // open: gs, en_out, en_in
  Comparator #(.mode("unsigned"), .width(9)) comparator_6 (
    .a({Inst9[8], Inst}), .b(9'h3c), .eq(comparator_6_eq));  // open: gt, lt
  Comparator #(.mode("unsigned"), .width(9)) comparator_7 (
    .a({Inst9[8], Inst}), .b(9'h3d), .eq(comparator_7_eq));  // open: gt, lt
  Register u_PrevInst (.D(Inst), .en(1'b1), .clk(CLK), .Q(PrevInst));  // open: clr
  Register #(.width(1)) TwoPart (.D(and_1_out), .en(1'b1), .clk(CLK), .Q(Inst9[8]));  // open: clr
  and and_1 (and_1_out, IS_LONG, ~Inst9[8]);  // AND_Gate
  or or_2 (WE_TI1, comparator_6_eq, comparator_7_eq);
  Comparator #(.mode("unsigned"), .width(9)) comparator_8 (
    .a({Inst9[8], Inst}), .b(9'h38), .eq(comparator_8_eq));  // open: gt, lt
  Comparator #(.mode("unsigned"), .width(9)) comparator_9 (
    .a({Inst9[8], Inst}), .b(9'h39), .eq(comparator_9_eq));  // open: gt, lt
  SecondInstUnit secondinstunit_1 (
    .PrevInst(PrevInst), .Inst(Inst), .PC(PC), .WE_RM(WE_RM2), .WE_ACC(WE_AC2), .WE_CF(WE_CF2),
    .WE_TEMP(WE_TE2), .WE_TIME(WE_TI2), .Choice_RM(C_RM2), .Source_PC(PC_SRC2), .Opcode_ALU(OP2),
    .PCImm(PCImm), .Shutdown(Shut), .OP_Branch(OP_Branch));
  Priority_Encoder #(.select(2)) priority_encoder_2 (
    .in0(1'b1), .in1(comparator_8_eq), .in2(comparator_9_eq), .out(TE_TIME_t));  // open: in3, gs, en_out, en_in
  Comparator #(.mode("unsigned"), .width(9)) comparator_10 (
    .a({Inst9[8], Inst}), .b(9'h2e), .eq(comparator_10_eq));  // open: gt, lt
  Comparator #(.mode("unsigned"), .width(9)) comparator_11 (
    .a({Inst9[8], Inst}), .b(9'h2f), .eq(comparator_11_eq));  // open: gt, lt
  or or_3 (or_3_out, comparator_10_eq, comparator_11_eq);
  Priority_Encoder priority_encoder_3 (
    .in0(1'b1), .in1(or_3_out), .out(PC_SRC1));  // open: in2, in3, in4, in5, in6, in7, en_in, gs, en_out
  Multiplexer multiplexer_1 (.in0(WE_RM1), .in1(WE_RM2), .out(WE_RM), .sel(Inst9[8]));
  Multiplexer multiplexer_2 (.in0(WE_AC1), .in1(WE_AC2), .out(WE_ACC), .sel(Inst9[8]));
  Multiplexer multiplexer_3 (.in0(WE_CF1), .in1(WE_CF2), .out(WE_CF), .sel(Inst9[8]));
  Multiplexer multiplexer_4 (.in0(WE_TE1), .in1(WE_TE2), .out(WE_TEMP), .sel(Inst9[8]));
  Multiplexer multiplexer_5 (.in0(WE_TI1), .in1(WE_TI2), .out(WE_TIME), .sel(Inst9[8]));
  Multiplexer #(.width(3)) multiplexer_6 (.in0(C_RM1), .in1(C_RM2), .out(Choice_RM), .sel(Inst9[8]));
  Multiplexer #(.width(3)) multiplexer_7 (.in0(PC_SRC1), .in1(PC_SRC2), .out(Source_PC), .sel(Inst9[8]));
  Multiplexer #(.width(8)) multiplexer_8 (.in0(OP1), .in1(OP2), .out(Opcode_ALU), .sel(Inst9[8]));
  Multiplexer multiplexer_9 (.in0(1'b0), .in1(Shut), .out(Shutdown), .sel(Inst9[8]));
  Multiplexer #(.width(2)) multiplexer_10 (.in0(WDE_IO), .in1(2'b00), .out(WDest_IO), .sel(Inst9[8]));
  Multiplexer #(.width(2)) multiplexer_11 (.in0(TE_TIME_t), .in1(2'b00), .out(TE_TIME), .sel(Inst9[8]));

  assign Inst9[7:0] = Inst;

  // Other names for the same wires on the sheet: IsSecond = Inst9[8]

  // Notes on the sheet:
  //   contents of rom_1 (hex, n*v repeats v):
  //   2 102 206 306 cc2 8c1 ce2 8e1 10c6 11c6 12c6 13c6 dc1 fc1 de1 fe1 d01 f01 d21 f21 d41 f41 d61 f61
  //   d81 f81 18c2 19c2 1ac2 18c1 19c1 1ac1 801 c02 821 c22 841 c42 861 c62 881 c82 404 504 600 700 0 4
  //   3002 902 3002 800 800 0 2006 10 0 0 2802 2902 2a00 2b00 0 b02 5*10 0 10 10 8*0 d011 d111 d211 d311
  //   d411 d511 d611 d711 d811 d911 da11 db11 dc11 dd11 de11 df11 d051 d151 d251 d351 d451 d551 d651 d751
  //   d851 d951 da51 db51 dc51 dd51 de51 df51 d002 d102 d202 d302 d402 d502 d602 d702 d802 d902 da02 db02
  //   dc02 dd02 de02 df02 128*10
  //   DO NOT CHANGE
  //   WE_TEMP
  //   WDE_IO
  //   WE_TIME
  //   TE_TIME
  //   PC_SRC
endmodule

module SecondInstUnit (
  input  [7:0] PrevInst,
  input  [7:0] Inst,
  input  [15:0] PC,
  output WE_RM,
  output WE_ACC,
  output WE_CF,
  output WE_TEMP,
  output WE_TIME,
  output [2:0] Choice_RM,
  output [2:0] Source_PC,
  output [7:0] Opcode_ALU,
  output [15:0] PCImm,
  output Shutdown,
  output [3:0] OP_Branch
);

  wire ACCALUF, BranchF, CallF, comparator_1_eq, comparator_2_eq, comparator_3_gt, comparator_4_lt,
       comparator_7_gt, comparator_8_lt, comparator_9_gt, comparator_10_lt, comparator_12_gt,
       comparator_13_gt, SetMemF, SetR4F, SetTIMEF;
  wire [2:0] multiplexer_4_out;
  wire [3:0] OpType;

  Comparator #(.mode("unsigned")) comparator_1 (.a(PrevInst), .b(8'h37), .eq(comparator_1_eq));  // open: gt, lt
  and and_1 (Shutdown, comparator_1_eq, comparator_2_eq);
  Comparator #(.mode("unsigned")) comparator_2 (.a(Inst), .b(8'h3e), .eq(comparator_2_eq));  // open: gt, lt
  Comparator #(.mode("unsigned")) comparator_3 (.a(PrevInst), .b(8'h3f), .gt(comparator_3_gt));  // open: eq, lt
  Comparator #(.mode("unsigned")) comparator_4 (.a(PrevInst), .b(8'h45), .lt(comparator_4_lt));  // open: gt, eq
  Comparator #(.mode("unsigned")) comparator_5 (.a(PrevInst), .b(8'h46), .eq(SetR4F));  // open: gt, lt
  Comparator #(.mode("unsigned")) comparator_6 (.a(PrevInst), .b(8'h47), .eq(SetTIMEF));  // open: gt, lt
  Comparator #(.mode("unsigned")) comparator_7 (.a(PrevInst), .b(8'h4f), .gt(comparator_7_gt));  // open: eq, lt
  Comparator #(.mode("unsigned")) comparator_8 (.a(PrevInst), .b(8'h70), .lt(comparator_8_lt));  // open: gt, eq
  Comparator #(.mode("unsigned")) comparator_9 (.a(PrevInst), .b(8'h7f), .gt(comparator_9_gt));  // open: eq, lt
  Comparator #(.mode("unsigned")) comparator_10 (.a(PrevInst), .b(8'he0), .lt(comparator_10_lt));  // open: gt, eq
  Comparator #(.mode("unsigned")) comparator_11 (.a(PrevInst), .b(8'hdf), .gt(CallF));  // open: eq, lt
  and and_2 (ACCALUF, comparator_3_gt, comparator_4_lt);
  and and_3 (SetMemF, comparator_7_gt, comparator_8_lt);
  and and_4 (BranchF, comparator_9_gt, comparator_10_lt);
  Comparator #(.mode("unsigned")) comparator_12 (.a(PrevInst), .b(8'hef), .gt(comparator_12_gt));  // open: eq, lt
  Multiplexer #(.select(4)) multiplexer_1 (
    .in0(1'b0), .in1(1'b0), .in2(1'b1), .in3(1'b0), .in4(1'b1), .in5(1'b0), .in6(1'b0), .out(WE_RM),
    .sel(OpType));  // open: in7, in8, in9, in10, in11, in12, in13, in14, in15
  Multiplexer #(.select(4)) multiplexer_2 (
    .in0(1'b0), .in1(1'b0), .in2(1'b0), .in3(1'b0), .in4(1'b0), .in5(1'b0), .in6(comparator_12_gt),
    .out(WE_TEMP), .sel(OpType));  // open: in7, in8, in9, in10, in11, in12, in13, in14, in15
  Comparator comparator_13 (.a(PrevInst), .b(8'h5f), .gt(comparator_13_gt));  // open: eq, lt
  // Probe on PCImm
  Multiplexer #(.select(4), .width(16)) multiplexer_3 (
    .in0({16{1'b0}}), .in1({16{1'b0}}), .in2({16{1'b0}}), .in3({16{1'b0}}), .in4({16{1'b0}}),
    .in5({PC[15:11], PrevInst[2:0], Inst}), .in6({PC[15:12], PrevInst[3:0], Inst}), .out(PCImm), .sel(OpType));  // open: in7, in8, in9, in10, in11, in12, in13, in14, in15
  Multiplexer #(.width(3)) multiplexer_4 (.in0(3'b001), .in1(3'b011), .out(multiplexer_4_out), .sel(comparator_13_gt));
  Priority_Encoder #(.select(4)) priority_encoder_1 (
    .in0(1'b1), .in1(ACCALUF), .in2(SetR4F), .in3(SetTIMEF), .in4(SetMemF), .in5(BranchF), .in6(CallF),
    .out(OpType));  // open: in7, in8, in9, in10, in11, in12, in13, in14, in15, gs, en_out, en_in
  Multiplexer #(.select(4)) multiplexer_5 (
    .in0(1'b0), .in1(1'b1), .in2(1'b0), .in3(1'b0), .in4(1'b0), .in5(1'b0), .in6(1'b0), .out(WE_ACC),
    .sel(OpType));  // open: in7, in8, in9, in10, in11, in12, in13, in14, in15
  Multiplexer #(.select(4)) multiplexer_6 (
    .in0(1'b0), .in1(1'b0), .in2(1'b0), .in3(1'b1), .in4(1'b0), .in5(1'b0), .in6(1'b0), .out(WE_TIME),
    .sel(OpType));  // open: in7, in8, in9, in10, in11, in12, in13, in14, in15
  Multiplexer #(.select(4), .width(3)) multiplexer_7 (
    .in0(3'b000), .in1(3'b000), .in2(3'b100), .in3(3'b000), .in4(multiplexer_4_out), .in5(3'b000),
    .in6(3'b000), .out(Choice_RM), .sel(OpType));  // open: in7, in8, in9, in10, in11, in12, in13, in14, in15
  Multiplexer #(.select(4), .width(8)) multiplexer_8 (
    .in0({8{1'b0}}), .in1({1'b1, PrevInst[2:0], Inst[3:0]}), .in2({4'b1101, Inst[3:0]}),
    .in3({4'b1101, Inst[3:0]}), .in4({4'b1101, Inst[3:0]}), .in5({8{1'b0}}), .in6({8{1'b0}}),
    .out(Opcode_ALU), .sel(OpType));  // open: in7, in8, in9, in10, in11, in12, in13, in14, in15
  Multiplexer #(.select(4), .width(3)) multiplexer_9 (
    .in0(3'b000), .in1(3'b000), .in2(3'b000), .in3(3'b000), .in4(3'b000), .in5(3'b010), .in6(3'b010),
    .out(Source_PC), .sel(OpType));  // open: in7, in8, in9, in10, in11, in12, in13, in14, in15
  // Probe on PrevInst[4:3]
  // Probe on Inst[3:0]
  // Probe on {PrevInst[2:0], Inst}
  // Probe on {PrevInst[3:0], Inst}

  assign OP_Branch = PrevInst[6:3];
  assign WE_CF = 1'b0;

  // Other names for the same wires on the sheet: Imm4[3:0] = Inst[3:0]; Imm11[10:0] = {PrevInst[2:0], Inst};
  //   Imm12[11:0] = {PrevInst[3:0], Inst}; Imm2[1:0] = PrevInst[4:3]; OpCode[7:0] = Opcode_ALU;
  //   PCSrc[2:0] = Source_PC; ShutF = Shutdown; WE_TE = WE_TEMP; WE_TI = WE_TIME
endmodule

module InstValidator (
  input  [7:0] Inst,
  output IsValid
);

  wire comparator_1_lt, comparator_2_eq, comparator_3_eq, comparator_4_eq;

  Comparator comparator_1 (.a(Inst), .b(8'h2a), .lt(comparator_1_lt));  // open: gt, eq
  Comparator comparator_2 (.a(Inst), .b(8'h31), .eq(comparator_2_eq));  // open: gt, lt
  Comparator comparator_3 (.a(Inst), .b(8'h3e), .eq(comparator_3_eq));  // open: gt, lt
  Comparator comparator_4 (.a(Inst), .b(8'h3f), .eq(comparator_4_eq));  // open: gt, lt
  or or_1 (IsValid, comparator_1_lt, comparator_2_eq, comparator_3_eq, comparator_4_eq);
endmodule

module InstMem (
  input  [15:0] Address,
  output [7:0] Inst
);

  ROM #(.addrWidth(16)) rom_1 (.addr(Address), .data(Inst));
  LED led_1 (.in(Inst[7]));
  LED led_2 (.in(Inst[6]));
  LED led_3 (.in(Inst[5]));
  LED led_4 (.in(Inst[4]));
  LED led_5 (.in(Inst[3]));
  LED led_6 (.in(Inst[2]));
  LED led_7 (.in(Inst[1]));
  LED led_8 (.in(Inst[0]));

  // Notes on the sheet:
  //   contents of rom_1 (hex, n*v repeats v):
  //   7c 60 9 7 61 9 7 62 9 7 7d 63 9 7 64 9 7 65 9 7 7e 66 9 7 67 9 7 75 60 a 7 7a 61 a 7 7f 62 a 7 74 63
  //   a 7 79 64 a 7 7e 65 a 7 73 66 a 7 78 67 a 7 70 50 c 5 10 a0 3e 70 50 d 5 10 a0 45 70 50 e 5 10 a0 4c
  //   70 50 f 5 70 51 f 5 e0 5a 7f 60 c 7 61 c 7 62 c 7 63 c 7 64 c 7 67 c 7 6c c 7 61 d 7 66 d 7 6b d 7
  //   60 e 7 65 e 7 6a e 7 6d e 7 6e e 7 6f e 7 60 f 7 61 f 7 71 50 8 5 75 57 8 5 70 58 8 5 59 8 5 76 6d c
  //   7 66 e 7 79 62 d 7 67 d 7 6c d 7 61 e 7 76 6e c 7 67 e 7 79 63 d 7 68 d 7 6d d 7 62 e 7 73 51 8 5 52
  //   8 5 73 53 8 5 71 54 8 5 7e 54 d 5 73 50 0 5 71 50 4 5 73 51 0 5 72 51 4 5 73 52 0 5 73 52 4 5 70 53
  //   b 5 72 54 b 5 70 55 b 5 56 b 5 73 55 8 5 75 56 8 5 72 55 d 5 e1 10 71 e1 1d e1 23 e1 8e e5 b7 e4 57
  //   e1 10 32 60 b 7 e1 13 50 b 4 b1 8a e1 2a 50 b 71 1b b9 36 70 50 8 5 e1 8c 50 b 72 1b b9 42 72 50 8 5
  //   e1 8c 50 b 74 1b b9 4e 73 50 8 5 e1 8c 50 b 78 1b b9 5a 71 50 8 5 e1 8c 50 b 79 1b b9 66 70 50 8 5
  //   e1 8c 50 b 75 1b b9 72 70 50 8 5 e1 8c 50 b 7a 1b b9 7e 72 50 8 5 e1 8c 50 b 76 1b b9 8a 72 50 8 5
  //   e1 8c e1 15 e1 15 51 8 4 20 52 8 4 22 50 8 4 24 25 b1 ab 41 1 b1 b6 41 1 b1 c3 41 1 b1 d0 e7 de 61 8
  //   6 b7 dc 6 41 1 7 e1 db 62 8 6 41 7 b7 dc 6 40 1 7 e1 db 61 8 6 41 7 b7 dc 6 40 1 7 e1 db 62 8 6 b7
  //   dc 6 41 1 7 e1 db 61 8 6 20 62 8 6 22 21 6a a 7 23 6b a 7 79 22 6a a 6 20 4 6c a 7 7a 22 6a a 6 20 4
  //   6d a 7 74 61 b 7 6b a 6 68 a 7 51 b b ca 26 71 5d a 2a 9 5 70 5c a 8 5 74 61 b 7 6b a 6 51 b b 68 a
  //   7 6c a 6 22 6d a 6 20 71 1a 61 b 7 71 51 b 1b b2 7c e2 3b 6c a 6 22 6d a 6 20 72 1a 61 b 7 72 51 b
  //   1b b2 84 e2 50 6c a 6 22 6d a 6 20 74 1a 61 b 7 74 51 b 1b b2 8c e2 65 6c a 6 22 6d a 6 20 78 1a 61
  //   b 7 78 51 b 1b b2 94 e2 7a e2 b8 70 58 a 1b b2 9c e2 3b 71 58 a 1b b2 9c e2 50 72 58 a 1b b2 9c e2
  //   65 73 58 a 1b b2 9c e2 7a 6a a 6 20 6b a 6 22 e2 a6 6a a 6 55 8 1b bf da 6b a 6 56 8 1b bf da e2 b8
  //   6a a 6 55 8 1b bb 79 6b a 6 56 8 1b bb 79 e2 ca e2 cc 71 59 8 2a 9 5 70 58 8 8 5 7f 65 8 7 66 8 7 e2
  //   e0 e2 e2 70 58 a 1b b3 2 e2 ea 71 58 a 1b b3 e e2 f2 72 58 a 1b b3 1a e2 fa 73 58 a 1b b3 26 e7 de
  //   6c a 6 22 6d a 6 20 71 1f e3 32 6c a 6 22 6d a 6 20 72 1f e3 32 6c a 6 22 6d a 6 20 74 1f e3 32 6c a
  //   6 22 6d a 6 20 78 1f e3 32 6a a 6 61 8 7 6b a 6 62 8 7 e3 40 71 54 b 2a 9 5 70 53 b 8 5 74 53 b 1b
  //   bb 5e 70 54 b 1b bb 5e 70 53 b 5 54 b 5 63 b 6 22 64 b 6 20 6a a 6 5 74 53 b 9 22 64 b 6 20 6b a 6 5
  //   e1 17 e3 7b 79 22 63 8 6 20 4 6e a 7 7a 22 63 8 6 20 4 6f a 7 74 61 b 7 64 8 6 69 a 7 51 b b cb b8
  //   71 5f a 2a 9 5 70 5e a 8 5 74 61 b 7 64 8 6 51 b b 69 a 7 e3 b8 70 59 a 1b b3 d8 e3 c0 71 59 a 1b b3
  //   e4 e3 c8 72 59 a 1b b3 f0 e3 d0 73 59 a 1b b3 fc e7 de 6e a 6 22 6f a 6 20 7e 1d e4 8 6e a 6 22 6f a
  //   6 20 7d 1d e4 8 6e a 6 22 6f a 6 20 7b 1d e4 8 6e a 6 22 6f a 6 20 77 1d e4 8 65 b 6 22 66 b 6 20 70
  //   5 74 55 b 9 22 66 b 6 20 70 5 71 56 b 2a 9 5 70 55 b 8 5 74 55 b 1b bc 3b 70 56 b 1b bc 3b 70 55 b 5
  //   56 b 5 65 b 6 22 66 b 6 20 4 63 8 7 74 55 b 2a 9 22 66 b 6 20 4 64 8 7 e2 e0 65 8 6 41 f b9 1b e4 60
  //   61 8 6 61 b 7 6 51 b 9 9 61 b 7 63 8 6 62 b 7 6 52 b 4*9 51 b 9 50 8 9 59 8 9 42 7 61 b 7 62 8 6 62
  //   b 7 6 52 b 6*9 62 b 7 64 8 6 67 b 7 6 57 b 9 9 52 b 9 51 b 9 59 8 9 42 7 62 b 7 e4 b6 61 b 6 20 62 b
  //   6 22 21 6a a 7 23 6b a 7 79 22 6a a 6 20 4 6c a 7 7a 22 6a a 6 20 4 6d a 7 74 67 b 7 6b a 6 68 a 7
  //   57 b b cd 1 71 5d a 2a 9 5 70 5c a 8 5 74 67 b 7 6b a 6 57 b b 68 a 7 70 58 a 1b bd 14 6c a 6 22 6d
  //   a 6 20 4 85 4d e5 65 71 58 a 1b bd 27 6c a 6 22 6d a 6 20 4 8d 4d e5 65 72 58 a 1b bd 3a 6c a 6 22
  //   6d a 6 20 4 95 4d e5 65 73 58 a 1b bf de 6c a 6 22 6d a 6 20 4 9d 4d e5 65 62 b 6 40 1 42 7 62 b 7
  //   bc b6 61 b 6 40 1 42 7 61 b 7 e4 b6 61 b 6 65 8 7 62 b 6 66 8 7 e5 73 70 58 a 1b b5 87 71 58 a 1b b5
  //   93 72 58 a 1b b5 9f e5 ab 6c a 6 22 6d a 6 20 71 1f e1 1b 6c a 6 22 6d a 6 20 72 1f e1 1b 6c a 6 22
  //   6d a 6 20 74 1f e1 1b 6c a 6 22 6d a 6 20 78 1f e1 1b 71 58 8 1b b7 de 70 59 8 1b b6 1f 71 59 8 1b
  //   b6 49 72 59 8 1b b6 62 73 59 8 1b b6 7c 74 59 8 1b b6 96 75 59 8 1b b6 ae 76 59 8 1b b6 c8 77 59 8
  //   1b b6 e2 78 59 8 1b b6 fa 79 59 8 1b b7 14 7a 59 8 1b b7 2e 7b 59 8 1b b7 5b 7c 59 8 1b b7 74 7d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
endmodule

module RegMemFile (
  input  CLK,
  input  WriteEnable,
  input  [3:0] WriteData,
  input  [2:0] RegChoice,
  output [3:0] DataOut,
  output [3:0] RA_Out,
  output [3:0] RB_Out,
  output [3:0] RD_Out,
  output [7:0] Mem_Addr
);

  wire or_1_out, WMBA, WMDC, WRA, WRB, WRC, WRD, WRE, WRF;
  wire [3:0] D_DC, DRE, MemData;

  Demultiplexer #(.select(3)) demultiplexer_1 (
    .out0(WRA), .out1(WRB), .out2(WRC), .out3(WRD), .out4(WRE), .out5(WRF), .out6(WMBA), .out7(WMDC),
    .in(WriteEnable), .sel(RegChoice));
  Register #(.width(4)) RA (.D(WriteData), .en(WRA), .clk(CLK), .Q(RA_Out));  // open: clr
  Register #(.width(4)) RB (.D(WriteData), .en(WRB), .clk(CLK), .Q(RB_Out));  // open: clr
  Register #(.width(4)) RC (.D(WriteData), .en(WRC), .clk(CLK), .Q(D_DC));  // open: clr
  Register #(.width(4)) RD (.D(WriteData), .en(WRD), .clk(CLK), .Q(RD_Out));  // open: clr
  Register #(.width(4)) RE (.D(WriteData), .en(WRE), .clk(CLK), .Q(DRE));  // open: clr
  or or_1 (or_1_out, WMBA, WMDC);
  Multiplexer #(.select(3), .width(8)) multiplexer_1 (
    .in0({8{1'b0}}), .in1({8{1'b0}}), .in2({8{1'b0}}), .in3({8{1'b0}}), .in4({8{1'b0}}), .in5({8{1'b0}}),
    .in6({RB_Out, RA_Out}), .in7({RD_Out, D_DC}), .out(Mem_Addr), .sel(RegChoice));
  RAM #(.asyncread("true"), .dataWidth(4)) Memory (
    .addr(Mem_Addr), .we(or_1_out), .oe(1'b1), .clk(CLK), .din(WriteData), .dout(MemData));
  Multiplexer #(.select(3), .width(4)) multiplexer_2 (
    .in0(RA_Out), .in1(RB_Out), .in2(D_DC), .in3(RD_Out), .in4(DRE), .in6(MemData), .in7(MemData),
    .out(DataOut), .sel(RegChoice));  // open: in5
  // Probe on Mem_Addr
  // Probe on MemData

  // Other names for the same wires on the sheet: Choice[2:0] = RegChoice; D_BA[7:0] = {RB_Out, RA_Out};
  //   DRA[3:0] = RA_Out; DRB[3:0] = RB_Out; DRC[3:0] = D_DC; D_DC[7:4] = RD_Out; DRD[3:0] = RD_Out;
  //   WD[3:0] = WriteData; WE = WriteEnable
endmodule

module RegIOFile (
  input  CLK,
  input  [3:0] WData,
  output [3:0] IOA
);


  assign IOA = WData;

  // Notes on the sheet:
  //   This is equivalent to a register with asynchronous Write Enables
  //   Designed so that input reaches as fast as possible, as it is no longer gated by clock
endmodule

module TimerFile (
  input  CLK,
  input  [7:0] WData,
  input  WE,
  input  [1:0] TE,
  output Is_Enabled,
  output [7:0] Timer_Out,
  output Four_Done
);

  wire comparator_2_gt, comparator_3_gt, comparator_4_gt, comparator_5_gt, not_1_out, WRITE;
  wire [2:0] T4, T4_1, WD_T4;
  wire [7:0] TIMER_1, WD_TIMER;

  Register #(.width(3)) u_T4 (.D(WD_T4), .en(Is_Enabled), .clk(CLK), .Q(T4), .clr(not_1_out));
  Register TIMER (.D(WD_TIMER), .en(WRITE), .clk(CLK), .Q(Timer_Out));  // open: clr
  J_K_Flip_Flop TIME_ENABLED (.J(TE[0]), .K(TE[1]), .clk(CLK), .Q(Is_Enabled));  // open: Qn, preset, reset
  not not_1 (not_1_out, Is_Enabled);
  or or_1 (WRITE, Four_Done, WE);
  Comparator #(.mode("unsigned"), .width(3)) comparator_1 (.a(T4), .b(3'b100), .eq(Four_Done));  // open: gt, lt
  Adder #(.width(3)) adder_1 (.a(T4), .b(3'b001), .out(T4_1));  // open: cin, cout
  Multiplexer #(.width(3)) multiplexer_1 (.in0(T4_1), .in1(3'b001), .out(WD_T4), .sel(Four_Done));
  Adder adder_2 (.a(Timer_Out), .b(8'h1), .out(TIMER_1));  // open: cin, cout
  Multiplexer #(.width(8)) multiplexer_2 (.in0(TIMER_1), .in1(WData), .out(WD_TIMER), .sel(WE));
  LED led_1 (.in(comparator_2_gt));
  Comparator #(.mode("unsigned"), .width(3)) comparator_2 (.a(T4), .b(3'b000), .gt(comparator_2_gt));  // open: eq, lt
  LED led_2 (.in(comparator_3_gt));
  Comparator #(.mode("unsigned"), .width(3)) comparator_3 (.a(T4), .b(3'b001), .gt(comparator_3_gt));  // open: eq, lt
  LED led_3 (.in(comparator_4_gt));
  Comparator #(.mode("unsigned"), .width(3)) comparator_4 (.a(T4), .b(3'b010), .gt(comparator_4_gt));  // open: eq, lt
  LED led_4 (.in(comparator_5_gt));
  Comparator #(.mode("unsigned"), .width(3)) comparator_5 (.a(T4), .b(3'b011), .gt(comparator_5_gt));  // open: eq, lt

  // Other names for the same wires on the sheet: TEn[1:0] = TE; TIME_ENABLED = Is_Enabled; TIMER[7:0] = Timer_Out;
  //   WEn = WE
endmodule

module ALU (
  input  [7:0] Opcode,
  input  [3:0] Data_In,
  input  [3:0] ACC_In,
  input  CF_In,
  input  [7:0] Time_In,
  input  [3:0] IOA_In,
  output [3:0] Nibble_Out,
  output CF_Out,
  output [7:0] Timer_Out
);

  wire comparator_1_eq;
  wire [3:0] I_Log_Out, I_Set_Out, Log_Out, Pet_Out, Time_Out;
  wire [4:0] Bin_Out, Cop_Out, Turn_Out;
  wire [7:0] Timer_Out_t, TimeSet_Out;

  RotateALU rotatealu_1 (
    .SubOp(Opcode[2:0]), .ACC_In(ACC_In), .CF_In(CF_In), .ACC_Out(Turn_Out[3:0]), .CF_Out(Turn_Out[4]));
  PerturbALU perturbalu_1 (.SubOp(Opcode[2:0]), .Data_In(Data_In), .ACC_In(ACC_In), .ALU_Out(Pet_Out));
  CarryOpALU carryopalu_1 (
    .SubOp(Opcode[2:0]), .ACC_In(ACC_In), .Data_In(Data_In), .CF_In(CF_In), .ALU_Out(Cop_Out[3:0]),
    .CF_Out(Cop_Out[4]));
  LogicALU logicalu_1 (.SubOp(Opcode[2:0]), .Data_In(Data_In), .ACC_In(ACC_In), .ALU_Out(Log_Out));
  BinDecALU bindecalu_1 (
    .SubOp(Opcode[2:0]), .ACC_In(ACC_In), .CF_In(CF_In), .ACC_Out(Bin_Out[3:0]), .CF_Out(Bin_Out[4]));
  TimerALU timeralu_1 (.SubOp(Opcode[2:0]), .ACC_In(ACC_In), .Time_In(Time_In), .A_OUT(Time_Out), .T_OUT(Timer_Out_t));
  ImmLogicALU immlogicalu_1 (.Opcode(Opcode), .ACC_In(ACC_In), .ALU_Out(I_Log_Out));
  ImmSetALU immsetalu_1 (.Opcode(Opcode), .Time_In(Time_In), .Nib_OUT(I_Set_Out), .T_OUT(TimeSet_Out));
  Multiplexer #(.select(5), .width(5)) multiplexer_1 (
    .in0(Turn_Out), .in1({CF_In, Pet_Out}), .in2(Cop_Out), .in3({CF_In, Log_Out}), .in4(Bin_Out),
    .in5({CF_In, Time_Out}), .in6({CF_In, IOA_In}), .in16({CF_In, I_Log_Out}), .in17({CF_In, I_Log_Out}),
    .in18({CF_In, I_Log_Out}), .in19({CF_In, I_Log_Out}), .in20({CF_In, I_Log_Out}),
    .in21({CF_In, I_Log_Out}), .in22({CF_In, I_Log_Out}), .in23({CF_In, I_Log_Out}),
    .in24({CF_In, I_Log_Out}), .in25({CF_In, I_Log_Out}), .in26({CF_In, I_Set_Out}),
    .in27({CF_In, I_Set_Out}), .out({CF_Out, Nibble_Out}), .sel(Opcode[7:3]));  // open: in7, in8, in9, in10, in11, in12, in13, in14, in15, in28, in29, in30, in31
  Multiplexer #(.width(8)) multiplexer_2 (.in0(TimeSet_Out), .in1(Timer_Out_t), .out(Timer_Out), .sel(comparator_1_eq));
  Comparator #(.mode("unsigned"), .width(5)) comparator_1 (
    .a(Opcode[7:3]), .b(5'b00101), .eq(comparator_1_eq));  // open: gt, lt

  // Other names for the same wires on the sheet: AIN[3:0] = ACC_In; DIN[3:0] = Data_In; CIN = CF_In;
  //   I_Log_Out[4] = CF_In; I_Set_Out[4] = CF_In; In_and_Out[4:0] = {CF_In, IOA_In}; Log_Out[4] = CF_In;
  //   Pet_Out[4] = CF_In; Time_Out[4] = CF_In; OPFull[7:0] = Opcode; SubOP[2:0] = Opcode[2:0]; OP[4:0] = Opcode[7:3];
  //   TIN[7:0] = Time_In

  // Notes on the sheet:
  //   Opcode: 00000
  //   Opcode: 00001
  //   Opcode: 00002
  //   Opcode: 00003
  //   Opcode: 00004
  //   Opcode: 00005
  //   Opcode: 00006
endmodule

module RotateALU (
  input  [2:0] SubOp,
  input  [3:0] ACC_In,
  input  CF_In,
  output [3:0] ACC_Out,
  output CF_Out
);

  // Probe on {ACC_In[2:0], ACC_In[3]}
  // Probe on {ACC_In[0], ACC_In[3:1]}
  // Probe on {ACC_In, CF_In}
  // Probe on {ACC_In[0], CF_In, ACC_In[3:1]}
  Multiplexer #(.select(3), .width(5)) multiplexer_1 (
    .in0({CF_In, ACC_In[0], ACC_In[3:1]}), .in1({CF_In, ACC_In[2:0], ACC_In[3]}),
    .in2({ACC_In[0], CF_In, ACC_In[3:1]}), .in3({ACC_In, CF_In}), .in4({1'b0, ACC_In}), .in5({1'b1, ACC_In}),
    .out({CF_Out, ACC_Out}), .sel(SubOp));  // open: in6, in7

  // Other names for the same wires on the sheet: CIN = CF_In; RotL[4:0] = {CF_In, ACC_In[2:0], ACC_In[3]};
  //   RotLC[4:0] = {ACC_In, CF_In}; RotR[4:0] = {CF_In, ACC_In[0], ACC_In[3:1]};
  //   RotRC[4:0] = {ACC_In[0], CF_In, ACC_In[3:1]}; AIN[3:0] = ACC_In; ClearCF[3:0] = ACC_In; SetCF[3:0] = ACC_In

  // Notes on the sheet:
  //   Rotate Right
  //   Rotate Left
  //   Rotate Left (C)
  //   Rotate Right (C)
  //   Clear CF
  //   Set CF
endmodule

module PerturbALU (
  input  [2:0] SubOp,
  input  [3:0] Data_In,
  input  [3:0] ACC_In,
  output [3:0] ALU_Out
);

  wire [3:0] bit_extender_1_out, multiplexer_1_out;

  assign bit_extender_1_out = {{2{SubOp[1]}}, SubOp[1:0]};  // Bit_Extender bit_extender_1
  Multiplexer #(.width(4)) multiplexer_1 (.in0(ACC_In), .in1(Data_In), .out(multiplexer_1_out), .sel(SubOp[2]));
  // Probe on bit_extender_1_out
  Adder #(.width(4)) adder_1 (.a(bit_extender_1_out), .b(multiplexer_1_out), .out(ALU_Out));  // open: cin, cout

  // Other names for the same wires on the sheet: AIN[3:0] = ACC_In; DIN[3:0] = Data_In; SubOp_t[1:0] = SubOp[1:0];
  //   Decider = SubOp[2]
endmodule

module CarryOpALU (
  input  [2:0] SubOp,
  input  [3:0] ACC_In,
  input  [3:0] Data_In,
  input  CF_In,
  output [3:0] ALU_Out,
  output CF_Out
);

  wire AddCF, and_1_out, and_2_out, Include_C, SubCF;
  wire [3:0] AddOut, SubOut;
  wire [4:0] adder_2_out;
  wire [4:4] subtractor_1_out;

  // Probe on ACC_In
  // Probe on Data_In
  and and_1 (and_1_out, CF_In, Include_C);
  Adder #(.width(4)) adder_1 (.a(ACC_In), .b(Data_In), .out(AddOut), .cin(and_1_out), .cout(AddCF));
  not not_1 (Include_C, SubOp[0]);
  and and_2 (and_2_out, CF_In, Include_C);
  Adder #(.width(5)) adder_2 (.a({1'b0, ACC_In}), .b({5{1'b0}}), .out(adder_2_out), .cin(and_2_out));  // open: cout
  Multiplexer #(.width(4)) multiplexer_1 (.in0(AddOut), .in1(SubOut), .out(ALU_Out), .sel(SubOp[1]));
  Multiplexer multiplexer_2 (.in0(AddCF), .in1(SubCF), .out(CF_Out), .sel(SubOp[1]));
  // Probe on SubOut
  Subtractor #(.width(5)) subtractor_1 (
    .a(adder_2_out), .b({1'b0, Data_In}), .out({subtractor_1_out[4], SubOut}), .bout(SubCF));  // open: bin

  // Other names for the same wires on the sheet: AIN[3:0] = ACC_In; DIN[3:0] = Data_In; CIN = CF_In;
  //   Operation = SubOp[1]

  // Notes on the sheet:
  //   ADD
endmodule

module LogicALU (
  input  [2:0] SubOp,
  input  [3:0] Data_In,
  input  [3:0] ACC_In,
  output [3:0] ALU_Out
);

  wire [3:0] and_1_out, or_1_out, xor_1_out;

  assign or_1_out = ACC_In | Data_In;  // OR_Gate or_1, 4 bits wide
  assign xor_1_out = ACC_In ^ Data_In;  // XOR_Gate xor_1, 4 bits wide
  assign and_1_out = ACC_In & Data_In;  // AND_Gate and_1, 4 bits wide
  Multiplexer #(.select(3), .width(4)) multiplexer_1 (
    .in0(and_1_out), .in1(xor_1_out), .in2(or_1_out), .out(ALU_Out), .sel(SubOp));  // open: in3, in4, in5, in6, in7

  // Other names for the same wires on the sheet: AIN[3:0] = ACC_In; DIN[3:0] = Data_In
endmodule

module BinDecALU (
  input  [2:0] SubOp,
  input  [3:0] ACC_In,
  input  CF_In,
  output [3:0] ACC_Out,
  output CF_Out
);

  wire comparator_1_gt, Decider;
  wire [3:0] adder_1_out;

  Comparator #(.mode("unsigned"), .width(4)) comparator_1 (
    .a(ACC_In), .b(4'b1001), .gt(comparator_1_gt));  // open: eq, lt
  or or_1 (Decider, comparator_1_gt, CF_In);
  Adder #(.width(4)) adder_1 (.a(ACC_In), .b(4'b0110), .out(adder_1_out));  // open: cin, cout
  Multiplexer #(.width(4)) multiplexer_1 (.in0(ACC_In), .in1(adder_1_out), .out(ACC_Out), .sel(Decider));
  Multiplexer multiplexer_2 (.in0(CF_In), .in1(1'b1), .out(CF_Out), .sel(Decider));

  // Other names for the same wires on the sheet: AIN[3:0] = ACC_In; CIN = CF_In
endmodule

module TimerALU (
  input  [2:0] SubOp,
  input  [3:0] ACC_In,
  input  [7:0] Time_In,
  output [3:0] A_OUT,
  output [7:0] T_OUT
);

  Multiplexer #(.select(2), .width(4)) multiplexer_1 (
    .in0(Time_In[3:0]), .in1(Time_In[7:4]), .in2(ACC_In), .in3(ACC_In), .out(A_OUT), .sel(SubOp[1:0]));
  Multiplexer #(.select(2), .width(8)) multiplexer_2 (
    .in0(Time_In), .in1(Time_In), .in2({Time_In[7:4], ACC_In}), .in3({ACC_In, Time_In[3:0]}), .out(T_OUT),
    .sel(SubOp[1:0]));

  // Other names for the same wires on the sheet: TIN[7:0] = Time_In; AIN[3:0] = ACC_In; SubOp_t[1:0] = SubOp[1:0]
endmodule

module ImmLogicALU (
  input  [7:0] Opcode,
  input  [3:0] ACC_In,
  output [3:0] ALU_Out
);

  wire [3:0] adder_1_out, and_1_out, or_1_out, subtractor_1_out, xor_1_out;

  assign or_1_out = ACC_In | Opcode[3:0];  // OR_Gate or_1, 4 bits wide
  assign xor_1_out = ACC_In ^ Opcode[3:0];  // XOR_Gate xor_1, 4 bits wide
  assign and_1_out = ACC_In & Opcode[3:0];  // AND_Gate and_1, 4 bits wide
  Subtractor #(.width(4)) subtractor_1 (.a(ACC_In), .b(Opcode[3:0]), .out(subtractor_1_out));  // open: bin, bout
  Adder #(.width(4)) adder_1 (.a(ACC_In), .b(Opcode[3:0]), .out(adder_1_out));  // open: cin, cout
  Multiplexer #(.select(3), .width(4)) multiplexer_1 (
    .in0(adder_1_out), .in1(subtractor_1_out), .in2(and_1_out), .in3(xor_1_out), .in4(or_1_out),
    .out(ALU_Out), .sel(Opcode[6:4]));  // open: in5, in6, in7

  // Other names for the same wires on the sheet: AIN[3:0] = ACC_In; Imm[3:0] = Opcode[3:0]; SubOp[2:0] = Opcode[6:4]
endmodule

module ImmSetALU (
  input  [7:0] Opcode,
  input  [7:0] Time_In,
  output [3:0] Nib_OUT,
  output [7:0] T_OUT
);


  assign Nib_OUT = Opcode[3:0];
  assign T_OUT = {Time_In[7:4], Opcode[3:0]};

  // Other names for the same wires on the sheet: SubOp[2:0] = Opcode[6:4]; Imm[3:0] = Opcode[3:0]; TIN[7:0] = Time_In
endmodule

module BranchChecker (
  input  [3:0] OPBranch,
  input  [3:0] ACC,
  input  [3:0] RA,
  input  [3:0] RB,
  input  [3:0] RD,
  input  CF,
  input  T_ENABLED,
  output IsJump
);

  wire ACNZ, not_1_out, not_2_out, RANZ, RBNZ, RDNZ;

  or or_1 (ACNZ, ACC[0], ACC[1], ACC[2], ACC[3]);
  or or_2 (RANZ, RA[0], RA[1], RA[2], RA[3]);
  or or_3 (RBNZ, RB[0], RB[1], RB[2], RB[3]);
  or or_4 (RDNZ, RD[0], RD[1], RD[2], RD[3]);
  not not_1 (not_1_out, ACNZ);
  not not_2 (not_2_out, CF);
  Multiplexer #(.select(4)) multiplexer_1 (
    .in0(ACC[0]), .in1(ACC[1]), .in2(ACC[2]), .in3(ACC[3]), .in4(RANZ), .in5(RBNZ), .in6(not_1_out),
    .in7(ACNZ), .in8(not_2_out), .in9(CF), .in10(T_ENABLED), .in11(RDNZ), .in12(1'b1), .in13(1'b1),
    .in14(1'b1), .in15(1'b1), .out(IsJump), .sel(OPBranch));

  // Other names for the same wires on the sheet: OP[3:0] = OPBranch; T_EN = T_ENABLED
endmodule

module LEDFile (
  input  CLK,
  input  [7:0] Mem_Addr,
  input  [3:0] W_Data,
  input  WE,
  output [19:0] OUT_0,
  output [19:0] OUT_1,
  output [19:0] OUT_2,
  output [19:0] OUT_3,
  output [19:0] OUT_4,
  output [19:0] OUT_5,
  output [19:0] OUT_6,
  output [19:0] OUT_7,
  output [19:0] OUT_8,
  output [19:0] OUT_9
);

  wire and_2_out, and_3_out, and_4_out, and_5_out, comparator_1_eq, comparator_2_eq, comparator_3_eq,
       comparator_4_eq, WE_00, WE_0A, WE_0B, WE_0C, WE_0D, WE_0E, WE_0F, WE_01, WE_1A, WE_1B, WE_1C, WE_1D,
       WE_1E, WE_1F, WE_02, WE_2A, WE_2B, WE_2C, WE_2D, WE_2E, WE_2F, WE_03, WE_04, WE_05, WE_06, WE_07,
       WE_08, WE_09, WE_10, WE_11, WE_12, WE_13, WE_14, WE_15, WE_16, WE_17, WE_18, WE_19, WE_20, WE_21,
       WE_22, WE_23, WE_24, WE_25, WE_26, WE_27, WE_28, WE_29, WE_30, WE_31, WE_t;

  and and_1 (WE_t, Mem_Addr[6], Mem_Addr[7], WE);
  Comparator #(.mode("unsigned"), .width(2)) comparator_1 (
    .a(2'b00), .b(Mem_Addr[5:4]), .eq(comparator_1_eq));  // open: gt, lt
  Comparator #(.mode("unsigned"), .width(2)) comparator_2 (
    .a(2'b01), .b(Mem_Addr[5:4]), .eq(comparator_2_eq));  // open: gt, lt
  Comparator #(.mode("unsigned"), .width(2)) comparator_3 (
    .a(2'b10), .b(Mem_Addr[5:4]), .eq(comparator_3_eq));  // open: gt, lt
  Comparator #(.mode("unsigned"), .width(2)) comparator_4 (
    .a(2'b11), .b(Mem_Addr[5:4]), .eq(comparator_4_eq));  // open: gt, lt
  and and_2 (and_2_out, WE_t, comparator_1_eq);
  Demultiplexer #(.select(4)) demultiplexer_1 (
    .out0(WE_00), .out1(WE_01), .out2(WE_02), .out3(WE_03), .out4(WE_04), .out5(WE_05), .out6(WE_06),
    .out7(WE_07), .out8(WE_08), .out9(WE_09), .out10(WE_0A), .out11(WE_0B), .out12(WE_0C), .out13(WE_0D),
    .out14(WE_0E), .out15(WE_0F), .in(and_2_out), .sel(Mem_Addr[3:0]));
  and and_3 (and_3_out, WE_t, comparator_2_eq);
  Demultiplexer #(.select(4)) demultiplexer_2 (
    .out0(WE_10), .out1(WE_11), .out2(WE_12), .out3(WE_13), .out4(WE_14), .out5(WE_15), .out6(WE_16),
    .out7(WE_17), .out8(WE_18), .out9(WE_19), .out10(WE_1A), .out11(WE_1B), .out12(WE_1C), .out13(WE_1D),
    .out14(WE_1E), .out15(WE_1F), .in(and_3_out), .sel(Mem_Addr[3:0]));
  and and_4 (and_4_out, WE_t, comparator_3_eq);
  Demultiplexer #(.select(4)) demultiplexer_3 (
    .out0(WE_20), .out1(WE_21), .out2(WE_22), .out3(WE_23), .out4(WE_24), .out5(WE_25), .out6(WE_26),
    .out7(WE_27), .out8(WE_28), .out9(WE_29), .out10(WE_2A), .out11(WE_2B), .out12(WE_2C), .out13(WE_2D),
    .out14(WE_2E), .out15(WE_2F), .in(and_4_out), .sel(Mem_Addr[3:0]));
  and and_5 (and_5_out, WE_t, comparator_4_eq);
  Demultiplexer #(.select(4)) demultiplexer_4 (
    .out0(WE_30), .out1(WE_31), .in(and_5_out), .sel(Mem_Addr[3:0]));  // open: out2, out3, out4, out5, out6, out7, out8, out9, out10, out11, out12, out13, out14, out15
  Register #(.width(4)) register_1 (
    .D(W_Data), .en(WE_00), .clk(CLK), .Q({OUT_0[16], OUT_0[17], OUT_0[18], OUT_0[19]}));  // open: clr
  Register #(.width(4)) register_2 (
    .D(W_Data), .en(WE_01), .clk(CLK), .Q({OUT_0[12], OUT_0[13], OUT_0[14], OUT_0[15]}));  // open: clr
  Register #(.width(4)) register_3 (
    .D(W_Data), .en(WE_02), .clk(CLK), .Q({OUT_0[8], OUT_0[9], OUT_0[10], OUT_0[11]}));  // open: clr
  Register #(.width(4)) register_4 (
    .D(W_Data), .en(WE_03), .clk(CLK), .Q({OUT_0[4], OUT_0[5], OUT_0[6], OUT_0[7]}));  // open: clr
  Register #(.width(4)) register_5 (
    .D(W_Data), .en(WE_04), .clk(CLK), .Q({OUT_0[0], OUT_0[1], OUT_0[2], OUT_0[3]}));  // open: clr
  Register #(.width(4)) register_6 (
    .D(W_Data), .en(WE_19), .clk(CLK), .Q({OUT_5[16], OUT_5[17], OUT_5[18], OUT_5[19]}));  // open: clr
  Register #(.width(4)) register_7 (
    .D(W_Data), .en(WE_1A), .clk(CLK), .Q({OUT_5[12], OUT_5[13], OUT_5[14], OUT_5[15]}));  // open: clr
  Register #(.width(4)) register_8 (
    .D(W_Data), .en(WE_1B), .clk(CLK), .Q({OUT_5[8], OUT_5[9], OUT_5[10], OUT_5[11]}));  // open: clr
  Register #(.width(4)) register_9 (
    .D(W_Data), .en(WE_1C), .clk(CLK), .Q({OUT_5[4], OUT_5[5], OUT_5[6], OUT_5[7]}));  // open: clr
  Register #(.width(4)) register_10 (
    .D(W_Data), .en(WE_1D), .clk(CLK), .Q({OUT_5[0], OUT_5[1], OUT_5[2], OUT_5[3]}));  // open: clr
  Register #(.width(4)) register_11 (
    .D(W_Data), .en(WE_05), .clk(CLK), .Q({OUT_1[16], OUT_1[17], OUT_1[18], OUT_1[19]}));  // open: clr
  Register #(.width(4)) register_12 (
    .D(W_Data), .en(WE_06), .clk(CLK), .Q({OUT_1[12], OUT_1[13], OUT_1[14], OUT_1[15]}));  // open: clr
  Register #(.width(4)) register_13 (
    .D(W_Data), .en(WE_07), .clk(CLK), .Q({OUT_1[8], OUT_1[9], OUT_1[10], OUT_1[11]}));  // open: clr
  Register #(.width(4)) register_14 (
    .D(W_Data), .en(WE_08), .clk(CLK), .Q({OUT_1[4], OUT_1[5], OUT_1[6], OUT_1[7]}));  // open: clr
  Register #(.width(4)) register_15 (
    .D(W_Data), .en(WE_09), .clk(CLK), .Q({OUT_1[0], OUT_1[1], OUT_1[2], OUT_1[3]}));  // open: clr
  Register #(.width(4)) register_16 (
    .D(W_Data), .en(WE_1E), .clk(CLK), .Q({OUT_6[16], OUT_6[17], OUT_6[18], OUT_6[19]}));  // open: clr
  Register #(.width(4)) register_17 (
    .D(W_Data), .en(WE_1F), .clk(CLK), .Q({OUT_6[12], OUT_6[13], OUT_6[14], OUT_6[15]}));  // open: clr
  Register #(.width(4)) register_18 (
    .D(W_Data), .en(WE_20), .clk(CLK), .Q({OUT_6[8], OUT_6[9], OUT_6[10], OUT_6[11]}));  // open: clr
  Register #(.width(4)) register_19 (
    .D(W_Data), .en(WE_21), .clk(CLK), .Q({OUT_6[4], OUT_6[5], OUT_6[6], OUT_6[7]}));  // open: clr
  Register #(.width(4)) register_20 (
    .D(W_Data), .en(WE_22), .clk(CLK), .Q({OUT_6[0], OUT_6[1], OUT_6[2], OUT_6[3]}));  // open: clr
  Register #(.width(4)) register_21 (
    .D(W_Data), .en(WE_0A), .clk(CLK), .Q({OUT_2[16], OUT_2[17], OUT_2[18], OUT_2[19]}));  // open: clr
  Register #(.width(4)) register_22 (
    .D(W_Data), .en(WE_0B), .clk(CLK), .Q({OUT_2[12], OUT_2[13], OUT_2[14], OUT_2[15]}));  // open: clr
  Register #(.width(4)) register_23 (
    .D(W_Data), .en(WE_0C), .clk(CLK), .Q({OUT_2[8], OUT_2[9], OUT_2[10], OUT_2[11]}));  // open: clr
  Register #(.width(4)) register_24 (
    .D(W_Data), .en(WE_0D), .clk(CLK), .Q({OUT_2[4], OUT_2[5], OUT_2[6], OUT_2[7]}));  // open: clr
  Register #(.width(4)) register_25 (
    .D(W_Data), .en(WE_0E), .clk(CLK), .Q({OUT_2[0], OUT_2[1], OUT_2[2], OUT_2[3]}));  // open: clr
  Register #(.width(4)) register_26 (
    .D(W_Data), .en(WE_23), .clk(CLK), .Q({OUT_7[16], OUT_7[17], OUT_7[18], OUT_7[19]}));  // open: clr
  Register #(.width(4)) register_27 (
    .D(W_Data), .en(WE_24), .clk(CLK), .Q({OUT_7[12], OUT_7[13], OUT_7[14], OUT_7[15]}));  // open: clr
  Register #(.width(4)) register_28 (
    .D(W_Data), .en(WE_25), .clk(CLK), .Q({OUT_7[8], OUT_7[9], OUT_7[10], OUT_7[11]}));  // open: clr
  Register #(.width(4)) register_29 (
    .D(W_Data), .en(WE_26), .clk(CLK), .Q({OUT_7[4], OUT_7[5], OUT_7[6], OUT_7[7]}));  // open: clr
  Register #(.width(4)) register_30 (
    .D(W_Data), .en(WE_27), .clk(CLK), .Q({OUT_7[0], OUT_7[1], OUT_7[2], OUT_7[3]}));  // open: clr
  Register #(.width(4)) register_31 (
    .D(W_Data), .en(WE_0F), .clk(CLK), .Q({OUT_3[16], OUT_3[17], OUT_3[18], OUT_3[19]}));  // open: clr
  Register #(.width(4)) register_32 (
    .D(W_Data), .en(WE_10), .clk(CLK), .Q({OUT_3[12], OUT_3[13], OUT_3[14], OUT_3[15]}));  // open: clr
  Register #(.width(4)) register_33 (
    .D(W_Data), .en(WE_11), .clk(CLK), .Q({OUT_3[8], OUT_3[9], OUT_3[10], OUT_3[11]}));  // open: clr
  Register #(.width(4)) register_34 (
    .D(W_Data), .en(WE_12), .clk(CLK), .Q({OUT_3[4], OUT_3[5], OUT_3[6], OUT_3[7]}));  // open: clr
  Register #(.width(4)) register_35 (
    .D(W_Data), .en(WE_13), .clk(CLK), .Q({OUT_3[0], OUT_3[1], OUT_3[2], OUT_3[3]}));  // open: clr
  Register #(.width(4)) register_36 (
    .D(W_Data), .en(WE_28), .clk(CLK), .Q({OUT_8[16], OUT_8[17], OUT_8[18], OUT_8[19]}));  // open: clr
  Register #(.width(4)) register_37 (
    .D(W_Data), .en(WE_29), .clk(CLK), .Q({OUT_8[12], OUT_8[13], OUT_8[14], OUT_8[15]}));  // open: clr
  Register #(.width(4)) register_38 (
    .D(W_Data), .en(WE_2A), .clk(CLK), .Q({OUT_8[8], OUT_8[9], OUT_8[10], OUT_8[11]}));  // open: clr
  Register #(.width(4)) register_39 (
    .D(W_Data), .en(WE_2B), .clk(CLK), .Q({OUT_8[4], OUT_8[5], OUT_8[6], OUT_8[7]}));  // open: clr
  Register #(.width(4)) register_40 (
    .D(W_Data), .en(WE_2C), .clk(CLK), .Q({OUT_8[0], OUT_8[1], OUT_8[2], OUT_8[3]}));  // open: clr
  Register #(.width(4)) register_41 (
    .D(W_Data), .en(WE_14), .clk(CLK), .Q({OUT_4[16], OUT_4[17], OUT_4[18], OUT_4[19]}));  // open: clr
  Register #(.width(4)) register_42 (
    .D(W_Data), .en(WE_15), .clk(CLK), .Q({OUT_4[12], OUT_4[13], OUT_4[14], OUT_4[15]}));  // open: clr
  Register #(.width(4)) register_43 (
    .D(W_Data), .en(WE_16), .clk(CLK), .Q({OUT_4[8], OUT_4[9], OUT_4[10], OUT_4[11]}));  // open: clr
  Register #(.width(4)) register_44 (
    .D(W_Data), .en(WE_17), .clk(CLK), .Q({OUT_4[4], OUT_4[5], OUT_4[6], OUT_4[7]}));  // open: clr
  Register #(.width(4)) register_45 (
    .D(W_Data), .en(WE_18), .clk(CLK), .Q({OUT_4[0], OUT_4[1], OUT_4[2], OUT_4[3]}));  // open: clr
  Register #(.width(4)) register_46 (
    .D(W_Data), .en(WE_2D), .clk(CLK), .Q({OUT_9[16], OUT_9[17], OUT_9[18], OUT_9[19]}));  // open: clr
  Register #(.width(4)) register_47 (
    .D(W_Data), .en(WE_2E), .clk(CLK), .Q({OUT_9[12], OUT_9[13], OUT_9[14], OUT_9[15]}));  // open: clr
  Register #(.width(4)) register_48 (
    .D(W_Data), .en(WE_2F), .clk(CLK), .Q({OUT_9[8], OUT_9[9], OUT_9[10], OUT_9[11]}));  // open: clr
  Register #(.width(4)) register_49 (
    .D(W_Data), .en(WE_30), .clk(CLK), .Q({OUT_9[4], OUT_9[5], OUT_9[6], OUT_9[7]}));  // open: clr
  Register #(.width(4)) register_50 (
    .D(W_Data), .en(WE_31), .clk(CLK), .Q({OUT_9[0], OUT_9[1], OUT_9[2], OUT_9[3]}));  // open: clr

  // Other names for the same wires on the sheet: MA[7:0] = Mem_Addr; MUX_S[3:0] = Mem_Addr[3:0];
  //   MUX_Ch[1:0] = Mem_Addr[5:4];
  //   OUT_0_t[19:0] = {OUT_0[0], OUT_0[1], OUT_0[2], OUT_0[3], OUT_0[4], OUT_0[5], OUT_0[6], OUT_0[7], OUT_0[8], OUT_0[9], OUT_0[10], OUT_0[11], OUT_0[12], OUT_0[13], OUT_0[14], OUT_0[15], OUT_0[16], OUT_0[17], OUT_0[18], OUT_0[19]};
  //   OUT_1_t[19:0] = {OUT_1[0], OUT_1[1], OUT_1[2], OUT_1[3], OUT_1[4], OUT_1[5], OUT_1[6], OUT_1[7], OUT_1[8], OUT_1[9], OUT_1[10], OUT_1[11], OUT_1[12], OUT_1[13], OUT_1[14], OUT_1[15], OUT_1[16], OUT_1[17], OUT_1[18], OUT_1[19]};
  //   OUT_2_t[19:0] = {OUT_2[0], OUT_2[1], OUT_2[2], OUT_2[3], OUT_2[4], OUT_2[5], OUT_2[6], OUT_2[7], OUT_2[8], OUT_2[9], OUT_2[10], OUT_2[11], OUT_2[12], OUT_2[13], OUT_2[14], OUT_2[15], OUT_2[16], OUT_2[17], OUT_2[18], OUT_2[19]};
  //   OUT_3_t[19:0] = {OUT_3[0], OUT_3[1], OUT_3[2], OUT_3[3], OUT_3[4], OUT_3[5], OUT_3[6], OUT_3[7], OUT_3[8], OUT_3[9], OUT_3[10], OUT_3[11], OUT_3[12], OUT_3[13], OUT_3[14], OUT_3[15], OUT_3[16], OUT_3[17], OUT_3[18], OUT_3[19]};
  //   OUT_4_t[19:0] = {OUT_4[0], OUT_4[1], OUT_4[2], OUT_4[3], OUT_4[4], OUT_4[5], OUT_4[6], OUT_4[7], OUT_4[8], OUT_4[9], OUT_4[10], OUT_4[11], OUT_4[12], OUT_4[13], OUT_4[14], OUT_4[15], OUT_4[16], OUT_4[17], OUT_4[18], OUT_4[19]};
  //   OUT_5_t[19:0] = {OUT_5[0], OUT_5[1], OUT_5[2], OUT_5[3], OUT_5[4], OUT_5[5], OUT_5[6], OUT_5[7], OUT_5[8], OUT_5[9], OUT_5[10], OUT_5[11], OUT_5[12], OUT_5[13], OUT_5[14], OUT_5[15], OUT_5[16], OUT_5[17], OUT_5[18], OUT_5[19]};
  //   OUT_6_t[19:0] = {OUT_6[0], OUT_6[1], OUT_6[2], OUT_6[3], OUT_6[4], OUT_6[5], OUT_6[6], OUT_6[7], OUT_6[8], OUT_6[9], OUT_6[10], OUT_6[11], OUT_6[12], OUT_6[13], OUT_6[14], OUT_6[15], OUT_6[16], OUT_6[17], OUT_6[18], OUT_6[19]};
  //   OUT_7_t[19:0] = {OUT_7[0], OUT_7[1], OUT_7[2], OUT_7[3], OUT_7[4], OUT_7[5], OUT_7[6], OUT_7[7], OUT_7[8], OUT_7[9], OUT_7[10], OUT_7[11], OUT_7[12], OUT_7[13], OUT_7[14], OUT_7[15], OUT_7[16], OUT_7[17], OUT_7[18], OUT_7[19]};
  //   OUT_8_t[19:0] = {OUT_8[0], OUT_8[1], OUT_8[2], OUT_8[3], OUT_8[4], OUT_8[5], OUT_8[6], OUT_8[7], OUT_8[8], OUT_8[9], OUT_8[10], OUT_8[11], OUT_8[12], OUT_8[13], OUT_8[14], OUT_8[15], OUT_8[16], OUT_8[17], OUT_8[18], OUT_8[19]};
  //   OUT_9_t[19:0] = {OUT_9[0], OUT_9[1], OUT_9[2], OUT_9[3], OUT_9[4], OUT_9[5], OUT_9[6], OUT_9[7], OUT_9[8], OUT_9[9], OUT_9[10], OUT_9[11], OUT_9[12], OUT_9[13], OUT_9[14], OUT_9[15], OUT_9[16], OUT_9[17], OUT_9[18], OUT_9[19]};
  //   WD[3:0] = W_Data
endmodule
